# Fritzing sketch barraSensoresJuntos (saved by Fritzing 0.9.2b)
circuit board: 8cm x 2.5cm
breadboards: 1

parts:
  J1 = female pin header, 24 pins [form="♀ (female)"]
  J2 = female pin header, 8 pins [form="♀ (female)"]
  J3 = female pin header, 2 pins [form="♀ (female)"]

nets:
  N1: J1.pin1, J1.pin4, J1.pin7, J1.pin10, J1.pin13, J1.pin16, J1.pin19, J1.pin22, J3.pin2
  N2: J1.pin2, J1.pin5, J1.pin8, J1.pin11, J1.pin14, J1.pin17, J1.pin20, J1.pin23, J3.pin1
  N3: J1.pin3, J2.pin1
  N4: J1.pin6, J2.pin2
  N5: J1.pin9, J2.pin3
  N6: J1.pin12, J2.pin4
  N7: J1.pin15, J2.pin5
  N8: J1.pin18, J2.pin6
  N9: J1.pin21, J2.pin7
  N10: J1.pin24, J2.pin8
