# Fritzing sketch barraSensoresSeparados (saved by Fritzing 0.9.2b)
circuit board: 8cm x 2.5cm
breadboards: 1

parts:
  J2 = female pin header, 8 pins [form="♀ (female)"]
  J3 = female pin header, 2 pins [form="♀ (female)"]
  J4 = female pin header, 3 pins [form="♀ (female)"]
  J5 = female pin header, 3 pins [form="♀ (female)"]

nets:
  N1: J2.pin8, J4.pin3
  N2: J3.pin1, J4.pin2, J5.pin3
  N3: J3.pin2, J4.pin1, J5.pin2
